// Logisim project CRC.circ as structural Verilog
module _4bit (
  input  [3:0] A,
  input  [3:0] B,
  output out_3,
  output [2:0] out_4
);

  wire [2:0] xor_1_out;

  // Probe on xor_1_out
  Multiplexer #(.width(3)) multiplexer_1 (.in0(A[2:0]), .in1(xor_1_out), .out(out_4), .sel(A[3]));  // open: en
  assign xor_1_out = A[2:0] ^ B[2:0];  // XOR_Gate xor_1, 3 bits wide

  assign out_3 = A[3];
endmodule

module CRC (
  input  [7:0] A,
  input  [3:0] B,
  output [10:0] out_3
);

  wire [2:0] n4bit_1_out_4, n4bit_2_out_4, n4bit_3_out_4, n4bit_4_out_4, n4bit_5_out_4, n4bit_6_out_4,
       n4bit_7_out_4;

  // Probe on A[7:4]
  _4bit u_4bit_1 (.A(A[7:4]), .B(B), .out_4(n4bit_1_out_4));  // open: out_3
  // Probe on n4bit_1_out_4
  _4bit u_4bit_2 (.A({n4bit_1_out_4, A[3]}), .B(B), .out_4(n4bit_2_out_4));  // open: out_3
  // Probe on n4bit_2_out_4
  _4bit u_4bit_3 (.A({n4bit_2_out_4, A[2]}), .B(B), .out_4(n4bit_3_out_4));  // open: out_3
  // Probe on n4bit_3_out_4
  _4bit u_4bit_4 (.A({n4bit_3_out_4, A[1]}), .B(B), .out_4(n4bit_4_out_4));  // open: out_3
  // Probe on n4bit_4_out_4
  _4bit u_4bit_5 (.A({n4bit_4_out_4, A[0]}), .B(B), .out_4(n4bit_5_out_4));  // open: out_3
  // Probe on n4bit_5_out_4
  _4bit u_4bit_6 (.A({n4bit_5_out_4, 1'b0}), .B(B), .out_4(n4bit_6_out_4));  // open: out_3
  // Probe on n4bit_6_out_4
  _4bit u_4bit_7 (.A({n4bit_6_out_4, 1'b0}), .B(B), .out_4(n4bit_7_out_4));  // open: out_3
  // Probe on n4bit_7_out_4
  _4bit u_4bit_8 (.A({n4bit_7_out_4, 1'b0}), .B(B), .out_4(out_3[2:0]));  // open: out_3
  // Probe on out_3[2:0]

  assign out_3[10:3] = A;
endmodule
