// Logisim project alu.circ as structural Verilog
module alu (
  input  [3:0] A,
  input  [3:0] B,
  input  [1:0] ALUOp,
  output [3:0] C
);

  wire [3:0] add_4bit_1_out_4, and_1_out, or_1_out, sub_1_out_3;

  add_4bit add_4bit_1 (.in_1(A), .in_2(1'b0), .in_3(B), .out_4(add_4bit_1_out_4));
  sub sub_1 (.in_1(A), .in_2(B), .out_3(sub_1_out_3));
  assign and_1_out = A & B;  // AND_Gate and_1, 4 bits wide
  assign or_1_out = A | B;  // OR_Gate or_1, 4 bits wide
  Multiplexer #(.select(2), .width(4)) multiplexer_1 (
    .in0(add_4bit_1_out_4), .in1(sub_1_out_3), .in2(and_1_out), .in3(or_1_out), .out(C), .sel(ALUOp));  // open: en
endmodule

module add_1bit (
  input  A,
  input  B,
  input  C,
  output out_4,
  output out_5
);

  wire and_1_out, and_2_out, and_3_out, and_4_out, and_5_out, and_6_out, and_7_out, not_1_out, not_2_out,
       not_3_out, not_4_out, not_5_out, not_6_out;

  not not_1 (not_1_out, B);
  not not_2 (not_2_out, C);
  not not_3 (not_3_out, A);
  not not_4 (not_4_out, C);
  not not_5 (not_5_out, A);
  not not_6 (not_6_out, B);
  and and_1 (and_1_out, A, B);
  and and_2 (and_2_out, A, C);
  and and_3 (and_3_out, B, C);
  and and_4 (and_4_out, A, B, C);
  and and_5 (and_5_out, A, not_1_out, not_2_out);
  and and_6 (and_6_out, not_3_out, B, not_4_out);
  and and_7 (and_7_out, not_5_out, not_6_out, C);
  or or_1 (out_4, and_1_out, and_2_out, and_3_out);
  or or_2 (out_5, and_4_out, and_5_out, and_6_out, and_7_out);
endmodule

module add_4bit (
  input  [3:0] in_1,
  input  in_2,
  input  [3:0] in_3,
  output [3:0] out_4
);

  wire add_1bit_1_out_4, add_1bit_2_out_4, add_1bit_4_out_4;

  add_1bit add_1bit_1 (.A(in_1[0]), .B(in_3[0]), .C(in_2), .out_4(add_1bit_1_out_4), .out_5(out_4[0]));
  add_1bit add_1bit_2 (.A(in_1[1]), .B(in_3[1]), .C(add_1bit_1_out_4), .out_4(add_1bit_2_out_4), .out_5(out_4[1]));
  add_1bit add_1bit_3 (.A(in_1[3]), .B(in_3[3]), .C(add_1bit_4_out_4), .out_5(out_4[3]));  // open: out_4
  add_1bit add_1bit_4 (.A(in_1[2]), .B(in_3[2]), .C(add_1bit_2_out_4), .out_4(add_1bit_4_out_4), .out_5(out_4[2]));
endmodule

module sub (
  input  [3:0] in_1,
  input  [3:0] in_2,
  output [3:0] out_3
);

  wire [3:0] not_1_out;

  assign not_1_out = ~in_2;  // NOT_Gate not_1, 4 bits wide
  add_4bit add_4bit_1 (.in_1(in_1), .in_2(1'b1), .in_3(not_1_out), .out_4(out_3));
endmodule
