// Logisim project CPU.circ as structural Verilog: 7 circuits, main circuit main
module main (
  input  in_1
);

  wire ALUSrc, clk, ExtOp, MemWrite, MentoReg, nPC_sel, RegDst, RegWrite, zero;
  wire [1:0] AluOp;
  wire [4:0] multiplexer_1_out;
  wire [31:0] alu_1_out_4, dm_1_rd, ext_1_ext32, grf_1_rd1, grf_1_rd2, ifu_1_out_5, multiplexer_2_out,
       multiplexer_3_out;

  Clock clock_1 (.out(clk));
  IFU ifu_1 (.IfBeq(nPC_sel), .zero(zero), .out_5(ifu_1_out_5), .clk(in_1), .reset(clk));
  Controller controller_1 (
    .RegDst(RegDst), .ALUSrc(ALUSrc), .MemtoReg(MentoReg), .RegWrite(RegWrite), .MemWrite(MemWrite),
    .nPC_sel(nPC_sel), .ExtOp(ExtOp), .AluOp(AluOp), .OpCode(ifu_1_out_5[31:26]), .Funct(ifu_1_out_5[5:0]));
  EXT ext_1 (.imm16(ifu_1_out_5[15:0]), .ExtOp(ExtOp), .ext32(ext_1_ext32));
  Multiplexer #(.width(5)) multiplexer_1 (
    .in0(ifu_1_out_5[20:16]), .in1(ifu_1_out_5[15:11]), .out(multiplexer_1_out), .sel(RegDst));  // open: en
  GRF grf_1 (
    .A1(ifu_1_out_5[25:21]), .A2(ifu_1_out_5[20:16]), .A3(multiplexer_1_out), .WD(multiplexer_3_out),
    .RD1(grf_1_rd1), .RD2(grf_1_rd2), .clk(clk), .reset(in_1), .WE(RegWrite));
  Multiplexer #(.width(32)) multiplexer_2 (
    .in0(grf_1_rd2), .in1(ext_1_ext32), .out(multiplexer_2_out), .sel(ALUSrc));  // open: en
  ALU alu_1 (.A(grf_1_rd1), .B(multiplexer_2_out), .AluOp(AluOp), .out_4(alu_1_out_4), .zero(zero));
  Multiplexer #(.width(32)) multiplexer_3 (
    .in0(alu_1_out_4), .in1(dm_1_rd), .out(multiplexer_3_out), .sel(MentoReg));  // open: en
  DM dm_1 (.A(alu_1_out_4), .WD(grf_1_rd2), .WE(MemWrite), .Clk(clk), .Reset(in_1), .RD(dm_1_rd));

  // Other names for the same wires on the sheet: reset = in_1
endmodule

module IFU (
  input  IfBeq,
  input  clk,
  input  reset,
  input  zero,
  output [31:0] out_5
);

  wire and_1_out;
  wire [31:0] adder_1_out, adder_2_out, adder_3_out, bit_extender_1_out, multiplexer_1_out, PC_q;

  assign bit_extender_1_out = {{16{1'b0}}, out_5[15:0]};  // Bit_Extender bit_extender_1
  Adder #(.width(32)) adder_1 (.a(PC_q), .b(bit_extender_1_out), .out(adder_1_out));  // open: cin, cout
  // Probe on adder_2_out
  Adder #(.width(32)) adder_2 (.a(PC_q), .b(32'h1), .out(adder_2_out));  // open: cin, cout
  Adder #(.width(32)) adder_3 (.a(32'h1), .b(adder_1_out), .out(adder_3_out));  // open: cin, cout
  and and_1 (and_1_out, IfBeq, zero);
  // Probe on adder_3_out
  Multiplexer #(.width(32)) multiplexer_1 (
    .in0(adder_2_out), .in1(adder_3_out), .out(multiplexer_1_out), .sel(and_1_out));  // open: en
  Register #(.width(32)) PC (.D(multiplexer_1_out), .Q(PC_q), .clk(clk), .clr(reset));  // open: en
  ROM #(.addrWidth(5), .dataWidth(32)) rom_1 (.addr(PC_q[4:0]), .data(out_5));  // open: sel
endmodule

module GRF (
  input  [4:0] A1,
  input  [4:0] A2,
  input  clk,
  input  reset,
  input  WE,
  input  [4:0] A3,
  input  [31:0] WD,
  output [31:0] RD1,
  output [31:0] RD2
);

  wire and_1_out, and_2_out, and_3_out, and_4_out, and_5_out, and_6_out, and_7_out, and_8_out, and_9_out,
       and_10_out, and_11_out, and_12_out, and_13_out, and_14_out, and_15_out, and_16_out, and_17_out,
       and_18_out, and_19_out, and_20_out, and_21_out, and_22_out, and_23_out, and_24_out, and_25_out,
       and_26_out, and_27_out, and_28_out, and_29_out, and_30_out, and_31_out, and_32_out, decoder_1_out0,
       decoder_1_out1, decoder_1_out2, decoder_1_out3, decoder_1_out4, decoder_1_out5, decoder_1_out6,
       decoder_1_out7, decoder_1_out8, decoder_1_out9, decoder_1_out10, decoder_1_out11, decoder_1_out12,
       decoder_1_out13, decoder_1_out14, decoder_1_out15, decoder_1_out16, decoder_1_out17, decoder_1_out18,
       decoder_1_out19, decoder_1_out20, decoder_1_out21, decoder_1_out22, decoder_1_out23, decoder_1_out24,
       decoder_1_out25, decoder_1_out26, decoder_1_out27, decoder_1_out28, decoder_1_out29, decoder_1_out30,
       decoder_1_out31;
  wire [31:0] _0, _1, _2, _3, _4, _5, _6, _7, _8, _9, _10, _11, _12, _13, _14, _15, _16, _17, _18, _19, _20,
       _21, _22, _23, _24, _25, _26, _27, _28, _29, _30, _31;

  Decoder #(.select(5)) decoder_1 (
    .out0(decoder_1_out0), .out1(decoder_1_out1), .out2(decoder_1_out2), .out3(decoder_1_out3),
    .out4(decoder_1_out4), .out5(decoder_1_out5), .out6(decoder_1_out6), .out7(decoder_1_out7),
    .out8(decoder_1_out8), .out9(decoder_1_out9), .out10(decoder_1_out10), .out11(decoder_1_out11),
    .out12(decoder_1_out12), .out13(decoder_1_out13), .out14(decoder_1_out14), .out15(decoder_1_out15),
    .out16(decoder_1_out16), .out17(decoder_1_out17), .out18(decoder_1_out18), .out19(decoder_1_out19),
    .out20(decoder_1_out20), .out21(decoder_1_out21), .out22(decoder_1_out22), .out23(decoder_1_out23),
    .out24(decoder_1_out24), .out25(decoder_1_out25), .out26(decoder_1_out26), .out27(decoder_1_out27),
    .out28(decoder_1_out28), .out29(decoder_1_out29), .out30(decoder_1_out30), .out31(decoder_1_out31),
    .sel(A3));  // open: en
  and and_1 (and_1_out, decoder_1_out0, WE);
  and and_2 (and_2_out, decoder_1_out1, WE);
  and and_3 (and_3_out, decoder_1_out2, WE);
  and and_4 (and_4_out, decoder_1_out3, WE);
  and and_5 (and_5_out, decoder_1_out4, WE);
  and and_6 (and_6_out, decoder_1_out5, WE);
  and and_7 (and_7_out, decoder_1_out6, WE);
  and and_8 (and_8_out, decoder_1_out7, WE);
  and and_9 (and_9_out, decoder_1_out8, WE);
  and and_10 (and_10_out, decoder_1_out9, WE);
  and and_11 (and_11_out, decoder_1_out10, WE);
  and and_12 (and_12_out, decoder_1_out11, WE);
  and and_13 (and_13_out, decoder_1_out12, WE);
  and and_14 (and_14_out, decoder_1_out13, WE);
  and and_15 (and_15_out, decoder_1_out14, WE);
  and and_16 (and_16_out, decoder_1_out15, WE);
  and and_17 (and_17_out, decoder_1_out16, WE);
  and and_18 (and_18_out, decoder_1_out17, WE);
  and and_19 (and_19_out, decoder_1_out18, WE);
  and and_20 (and_20_out, decoder_1_out19, WE);
  and and_21 (and_21_out, decoder_1_out20, WE);
  and and_22 (and_22_out, decoder_1_out21, WE);
  and and_23 (and_23_out, decoder_1_out22, WE);
  and and_24 (and_24_out, decoder_1_out23, WE);
  and and_25 (and_25_out, decoder_1_out24, WE);
  and and_26 (and_26_out, decoder_1_out25, WE);
  and and_27 (and_27_out, decoder_1_out26, WE);
  and and_28 (and_28_out, decoder_1_out27, WE);
  and and_29 (and_29_out, decoder_1_out28, WE);
  and and_30 (and_30_out, decoder_1_out29, WE);
  and and_31 (and_31_out, decoder_1_out30, WE);
  and and_32 (and_32_out, decoder_1_out31, WE);
  Register #(.width(32)) register_1 (.D(WD), .en(and_1_out), .Q(_0), .clk(clk), .clr(reset));
  Register #(.width(32)) register_2 (.D(WD), .en(and_2_out), .Q(_1), .clk(clk), .clr(reset));
  Register #(.width(32)) register_3 (.D(WD), .en(and_3_out), .Q(_2), .clk(clk), .clr(reset));
  Register #(.width(32)) register_4 (.D(WD), .en(and_4_out), .Q(_3), .clk(clk), .clr(reset));
  Register #(.width(32)) register_5 (.D(WD), .en(and_5_out), .Q(_4), .clk(clk), .clr(reset));
  Register #(.width(32)) register_6 (.D(WD), .en(and_6_out), .Q(_5), .clk(clk), .clr(reset));
  Register #(.width(32)) register_7 (.D(WD), .en(and_7_out), .Q(_6), .clk(clk), .clr(reset));
  Register #(.width(32)) register_8 (.D(WD), .en(and_8_out), .Q(_7), .clk(clk), .clr(reset));
  Register #(.width(32)) register_9 (.D(WD), .en(and_9_out), .Q(_8), .clk(clk), .clr(reset));
  Register #(.width(32)) register_10 (.D(WD), .en(and_10_out), .Q(_9), .clk(clk), .clr(reset));
  Register #(.width(32)) register_11 (.D(WD), .en(and_11_out), .Q(_10), .clk(clk), .clr(reset));
  Register #(.width(32)) register_12 (.D(WD), .en(and_12_out), .Q(_11), .clk(clk), .clr(reset));
  Register #(.width(32)) register_13 (.D(WD), .en(and_13_out), .Q(_12), .clk(clk), .clr(reset));
  Register #(.width(32)) register_14 (.D(WD), .en(and_14_out), .Q(_13), .clk(clk), .clr(reset));
  Register #(.width(32)) register_15 (.D(WD), .en(and_15_out), .Q(_14), .clk(clk), .clr(reset));
  Register #(.width(32)) register_16 (.D(WD), .en(and_16_out), .Q(_15), .clk(clk), .clr(reset));
  Register #(.width(32)) register_17 (.D(WD), .en(and_17_out), .Q(_16), .clk(clk), .clr(reset));
  Register #(.width(32)) register_18 (.D(WD), .en(and_18_out), .Q(_17), .clk(clk), .clr(reset));
  Register #(.width(32)) register_19 (.D(WD), .en(and_19_out), .Q(_18), .clk(clk), .clr(reset));
  Register #(.width(32)) register_20 (.D(WD), .en(and_20_out), .Q(_19), .clk(clk), .clr(reset));
  Register #(.width(32)) register_21 (.D(WD), .en(and_21_out), .Q(_20), .clk(clk), .clr(reset));
  Register #(.width(32)) register_22 (.D(WD), .en(and_22_out), .Q(_21), .clk(clk), .clr(reset));
  Register #(.width(32)) register_23 (.D(WD), .en(and_23_out), .Q(_22), .clk(clk), .clr(reset));
  Register #(.width(32)) register_24 (.D(WD), .en(and_24_out), .Q(_23), .clk(clk), .clr(reset));
  Register #(.width(32)) register_25 (.D(WD), .en(and_25_out), .Q(_24), .clk(clk), .clr(reset));
  Register #(.width(32)) register_26 (.D(WD), .en(and_26_out), .Q(_25), .clk(clk), .clr(reset));
  Register #(.width(32)) register_27 (.D(WD), .en(and_27_out), .Q(_26), .clk(clk), .clr(reset));
  Register #(.width(32)) register_28 (.D(WD), .en(and_28_out), .Q(_27), .clk(clk), .clr(reset));
  Register #(.width(32)) register_29 (.D(WD), .en(and_29_out), .Q(_28), .clk(clk), .clr(reset));
  Register #(.width(32)) register_30 (.D(WD), .en(and_30_out), .Q(_29), .clk(clk), .clr(reset));
  Register #(.width(32)) register_31 (.D(WD), .en(and_31_out), .Q(_30), .clk(clk), .clr(reset));
  Register #(.width(32)) register_32 (.D(WD), .en(and_32_out), .Q(_31), .clk(clk), .clr(reset));
  Multiplexer #(.select(5), .width(32)) multiplexer_1 (
    .in0(_0), .in1(_1), .in2(_2), .in3(_3), .in4(_4), .in5(_5), .in6(_6), .in7(_7), .in8(_8), .in9(_9),
    .in10(_10), .in11(_11), .in12(_12), .in13(_13), .in14(_14), .in15(_15), .in16(_16), .in17(_17),
    .in18(_18), .in19(_19), .in20(_20), .in21(_21), .in22(_22), .in23(_23), .in24(_24), .in25(_25),
    .in26(_26), .in27(_27), .in28(_28), .in29(_29), .in30(_30), .in31(_31), .out(RD1), .sel(A1));  // open: en
  Multiplexer #(.select(5), .width(32)) multiplexer_2 (
    .in0(_0), .in1(_1), .in2(_2), .in3(_3), .in4(_4), .in5(_5), .in6(_6), .in7(_7), .in8(_8), .in9(_9),
    .in10(_10), .in11(_11), .in12(_12), .in13(_13), .in14(_14), .in15(_15), .in16(_16), .in17(_17),
    .in18(_18), .in19(_19), .in20(_20), .in21(_21), .in22(_22), .in23(_23), .in24(_24), .in25(_25),
    .in26(_26), .in27(_27), .in28(_28), .in29(_29), .in30(_30), .in31(_31), .out(RD2), .sel(A2));  // open: en

  // Other names for the same wires on the sheet: data[31:0] = WD
endmodule

module ALU (
  input  [31:0] A,
  input  [31:0] B,
  input  [1:0] AluOp,
  output [31:0] out_4,
  output zero
);

  wire [31:0] adder_1_out, or_1_out, subtractor_1_out;

  assign or_1_out = A | B;  // OR_Gate or_1, 32 bits wide
  Subtractor #(.width(32)) subtractor_1 (.a(A), .b(B), .out(subtractor_1_out));  // open: bin, bout
  Adder #(.width(32)) adder_1 (.a(A), .b(B), .out(adder_1_out));  // open: cin, cout
  Multiplexer #(.select(2), .width(32)) multiplexer_1 (
    .in0(or_1_out), .in1(subtractor_1_out), .in2(adder_1_out), .out(out_4), .sel(AluOp));  // open: in3, en
  Comparator #(.width(32)) comparator_1 (.a(out_4), .b({32{1'b0}}), .eq(zero));  // open: gt, lt
endmodule

module DM (
  input  [31:0] A,
  input  [31:0] WD,
  input  WE,
  input  Clk,
  input  Reset,
  output [31:0] RD
);

  RAM #(.addrWidth(5), .dataWidth(32), .bus("separate")) ram_1 (
    .addr(A[6:2]), .din(WD), .data(RD), .str(WE), .clk(Clk), .clr(Reset));  // open: sel, ld
endmodule

module EXT (
  input  [15:0] imm16,
  input  ExtOp,
  output [31:0] ext32
);

  wire [31:0] bit_extender_1_out;

  assign bit_extender_1_out = {{16{1'b0}}, imm16};  // Bit_Extender bit_extender_1
  Multiplexer #(.width(32)) multiplexer_1 (
    .in0(bit_extender_1_out), .in1({imm16, {16{1'b0}}}), .out(ext32), .sel(ExtOp));  // open: en
endmodule

module Controller (
  input  [5:0] OpCode,
  input  [5:0] Funct,
  output RegDst,
  output ALUSrc,
  output MemtoReg,
  output RegWrite,
  output MemWrite,
  output nPC_sel,
  output ExtOp,
  output [1:0] AluOp
);

  wire add_out, nop_out, not_1_out, not_2_out, not_3_out, not_4_out, not_5_out, not_6_out, not_7_out,
       not_8_out, not_9_out, not_10_out, not_11_out, not_12_out, ori_out, sub_out;

  not not_1 (not_1_out, OpCode[5]);
  not not_2 (not_2_out, OpCode[2]);
  not not_3 (not_3_out, OpCode[1]);
  not not_4 (not_4_out, OpCode[3]);
  not not_5 (not_5_out, OpCode[4]);
  not not_6 (not_6_out, OpCode[0]);
  not not_7 (not_7_out, Funct[2]);
  not not_8 (not_8_out, Funct[3]);
  not not_9 (not_9_out, Funct[5]);
  not not_10 (not_10_out, Funct[4]);
  not not_11 (not_11_out, Funct[1]);
  not not_12 (not_12_out, Funct[0]);
  and add (add_out, not_1_out, not_5_out, not_4_out, not_2_out, not_3_out, not_6_out, Funct[5], not_10_out, not_8_out, not_7_out, not_11_out, not_12_out);
  and sub (sub_out, not_1_out, not_5_out, not_4_out, not_2_out, not_3_out, not_6_out, Funct[5], not_10_out, not_8_out, not_7_out, Funct[1], not_12_out);
  and ori (ori_out, not_1_out, not_5_out, OpCode[3], OpCode[2], not_3_out, OpCode[0]);
  and lw (MemtoReg, OpCode[5], not_5_out, not_4_out, not_2_out, OpCode[1], OpCode[0]);
  and sw (MemWrite, OpCode[5], not_5_out, OpCode[3], not_2_out, OpCode[1], OpCode[0]);
  and beq (nPC_sel, not_1_out, not_5_out, not_4_out, OpCode[2], not_3_out, not_6_out);
  and lui (ExtOp, not_1_out, not_5_out, OpCode[3], OpCode[2], OpCode[1], OpCode[0]);
  and nop (nop_out, not_1_out, not_5_out, not_4_out, not_2_out, not_3_out, not_6_out, not_9_out, not_10_out, not_8_out, not_7_out, not_11_out, not_12_out);
  or or_1 (RegDst, add_out, sub_out);
  or or_2 (ALUSrc, ori_out, MemtoReg, MemWrite, ExtOp);
  or or_3 (RegWrite, add_out, sub_out, ori_out, MemtoReg, ExtOp);
  or or_4 (AluOp[0], sub_out, nPC_sel);
  or or_5 (AluOp[1], add_out, MemtoReg, MemWrite);
endmodule
