// Logisim project CPU（第二版添加了J型指令）.circ as structural Verilog: 8 circuits, main circuit main
module main (
  input  in_1,
  output [31:0] out_2,
  output out_3,
  output [4:0] out_4,
  output [31:0] out_5,
  output out_6,
  output [4:0] out_7,
  output [31:0] out_8
);

  wire alu_1_zero, ALUSrc, Clk, controller_1_branch, J, MemtoReg, PCSrc;
  wire [1:0] ExtOp, Jump, RegDst;
  wire [3:0] ALUOp;
  wire [31:0] alu_1_c, dm_1_rd, ext_1_ext32, j_r, multiplexer_2_out, multiplexer_3_out, PC_4;

  IFU ifu_1 (.Clk(Clk), .Instr(out_2), .Reset(in_1), .PCSrc(PCSrc), .Jump(Jump), .PC_4(PC_4), .j_r(j_r), .J(J));
  // Probe on out_2
  Multiplexer #(.select(2), .width(5), .enable("false")) multiplexer_1 (
    .in0(out_2[20:16]), .in1(out_2[15:11]), .in2({5{1'b1}}), .out(out_4), .sel(RegDst));  // open: in3
  EXT ext_1 (.Imm16(out_2[15:0]), .ExtOp(ExtOp), .Ext32(ext_1_ext32));
  Controller controller_1 (
    .RegDst(RegDst), .ALUSrc(ALUSrc), .MemtoReg(MemtoReg), .RegWrite(out_3), .MemWrite(out_6),
    .Branch(controller_1_branch), .ExtOp(ExtOp), .ALUOp(ALUOp), .Op(out_2[31:26]), .Funct(out_2[5:0]),
    .Jump(Jump), .J(J));
  GRF grf_1 (
    .A3(out_4), .WD3(out_5), .RD1(j_r), .RD2(out_8), .Clk(Clk), .Reset(in_1), .RegWrite(out_3),
    .A1(out_2[25:21]), .A2(out_2[20:16]));
  and and_1 (PCSrc, controller_1_branch, alu_1_zero);
  Multiplexer #(.width(32), .enable("false")) multiplexer_2 (
    .in0(out_8), .in1(ext_1_ext32), .out(multiplexer_2_out), .sel(ALUSrc));
  // Probe on multiplexer_2_out
  // Probe on j_r
  ALU alu_1 (
    .A(j_r), .B(multiplexer_2_out), .C({alu_1_c[31:7], out_7, alu_1_c[1:0]}), .zero(alu_1_zero), .ALUOp(ALUOp));
  // Probe on {alu_1_c[31:7], out_7, alu_1_c[1:0]}
  Multiplexer #(.select(2), .width(32), .enable("false")) multiplexer_3 (
    .in0({alu_1_c[31:7], out_7, alu_1_c[1:0]}), .in1(PC_4), .in2(PC_4), .out(multiplexer_3_out), .sel(Jump));  // open: in3
  DM dm_1 (
    .A({alu_1_c[31:7], out_7, alu_1_c[1:0]}), .WD(out_8), .MemWrite(out_6), .Clk(Clk), .Reset(in_1),
    .RD(dm_1_rd));
  // Probe on multiplexer_3_out
  // Probe on dm_1_rd
  Multiplexer #(.width(32), .enable("false")) multiplexer_4 (
    .in0(multiplexer_3_out), .in1(dm_1_rd), .out(out_5), .sel(MemtoReg));
  Clock clock_1 (.out(Clk));

  // Other names for the same wires on the sheet: MemAddr[4:0] = out_7; Instr[31:0] = out_2; MemData[31:0] = out_8;
  //   MemWrite = out_6; RegAddr[4:0] = out_4; RegData[31:0] = out_5; RegWrite = out_3; Reset = in_1
endmodule

module GRF (
  input  RegWrite,
  input  Clk,
  input  Reset,
  input  [4:0] A1,
  input  [4:0] A3,
  input  [31:0] WD3,
  input  [4:0] A2,
  output [31:0] RD1,
  output [31:0] RD2
);

  wire and_2_out, and_3_out, and_4_out, and_5_out, and_6_out, and_7_out, and_8_out, and_9_out, and_10_out,
       and_11_out, and_12_out, and_13_out, and_14_out, and_15_out, and_16_out, and_17_out, and_18_out,
       and_19_out, and_20_out, and_21_out, and_22_out, and_23_out, and_24_out, and_25_out, and_26_out,
       and_27_out, and_28_out, and_29_out, and_30_out, and_31_out, and_32_out, decoder_1_out0,
       decoder_1_out1, decoder_1_out2, decoder_1_out3, decoder_1_out4, decoder_1_out5, decoder_1_out6,
       decoder_1_out7, decoder_1_out8, decoder_1_out9, decoder_1_out10, decoder_1_out11, decoder_1_out12,
       decoder_1_out13, decoder_1_out14, decoder_1_out15, decoder_1_out16, decoder_1_out17, decoder_1_out18,
       decoder_1_out19, decoder_1_out20, decoder_1_out21, decoder_1_out22, decoder_1_out23, decoder_1_out24,
       decoder_1_out25, decoder_1_out26, decoder_1_out27, decoder_1_out28, decoder_1_out29, decoder_1_out30,
       decoder_1_out31;
  wire [31:0] _0, _1, _2, _3, _4, _5, _6, _7, _8, _9, _10, _11, _12, _13, _14, _15, _16, _17, _18, _19, _20,
       _21, _22, _23, _24, _25, _26, _27, _28, _29, _30, _31;

  Decoder #(.select(5)) decoder_1 (
    .out0(decoder_1_out0), .out1(decoder_1_out1), .out2(decoder_1_out2), .out3(decoder_1_out3),
    .out4(decoder_1_out4), .out5(decoder_1_out5), .out6(decoder_1_out6), .out7(decoder_1_out7),
    .out8(decoder_1_out8), .out9(decoder_1_out9), .out10(decoder_1_out10), .out11(decoder_1_out11),
    .out12(decoder_1_out12), .out13(decoder_1_out13), .out14(decoder_1_out14), .out15(decoder_1_out15),
    .out16(decoder_1_out16), .out17(decoder_1_out17), .out18(decoder_1_out18), .out19(decoder_1_out19),
    .out20(decoder_1_out20), .out21(decoder_1_out21), .out22(decoder_1_out22), .out23(decoder_1_out23),
    .out24(decoder_1_out24), .out25(decoder_1_out25), .out26(decoder_1_out26), .out27(decoder_1_out27),
    .out28(decoder_1_out28), .out29(decoder_1_out29), .out30(decoder_1_out30), .out31(decoder_1_out31),
    .sel(A3));  // open: en
  // AND_Gate and_1 has open pins: in0=decoder_1_out0, in1=RegWrite, out=open
  and and_2 (and_2_out, decoder_1_out1, RegWrite);
  and and_3 (and_3_out, decoder_1_out2, RegWrite);
  and and_4 (and_4_out, decoder_1_out3, RegWrite);
  and and_5 (and_5_out, decoder_1_out4, RegWrite);
  and and_6 (and_6_out, decoder_1_out5, RegWrite);
  and and_7 (and_7_out, decoder_1_out6, RegWrite);
  and and_8 (and_8_out, decoder_1_out7, RegWrite);
  and and_9 (and_9_out, decoder_1_out8, RegWrite);
  and and_10 (and_10_out, decoder_1_out9, RegWrite);
  and and_11 (and_11_out, decoder_1_out10, RegWrite);
  and and_12 (and_12_out, decoder_1_out11, RegWrite);
  and and_13 (and_13_out, decoder_1_out12, RegWrite);
  and and_14 (and_14_out, decoder_1_out13, RegWrite);
  and and_15 (and_15_out, decoder_1_out14, RegWrite);
  and and_16 (and_16_out, decoder_1_out15, RegWrite);
  and and_17 (and_17_out, decoder_1_out16, RegWrite);
  and and_18 (and_18_out, decoder_1_out17, RegWrite);
  and and_19 (and_19_out, decoder_1_out18, RegWrite);
  and and_20 (and_20_out, decoder_1_out19, RegWrite);
  and and_21 (and_21_out, decoder_1_out20, RegWrite);
  and and_22 (and_22_out, decoder_1_out21, RegWrite);
  and and_23 (and_23_out, decoder_1_out22, RegWrite);
  and and_24 (and_24_out, decoder_1_out23, RegWrite);
  and and_25 (and_25_out, decoder_1_out24, RegWrite);
  and and_26 (and_26_out, decoder_1_out25, RegWrite);
  and and_27 (and_27_out, decoder_1_out26, RegWrite);
  and and_28 (and_28_out, decoder_1_out27, RegWrite);
  and and_29 (and_29_out, decoder_1_out28, RegWrite);
  and and_30 (and_30_out, decoder_1_out29, RegWrite);
  and and_31 (and_31_out, decoder_1_out30, RegWrite);
  and and_32 (and_32_out, decoder_1_out31, RegWrite);
  Register #(.width(32)) register_1 (.Q(_0), .clk(Clk), .clr(Reset));  // open: D, en
  Register #(.width(32)) register_2 (.D(WD3), .en(and_2_out), .Q(_1), .clk(Clk), .clr(Reset));
  Register #(.width(32)) register_3 (.D(WD3), .en(and_3_out), .Q(_2), .clk(Clk), .clr(Reset));
  Register #(.width(32)) register_4 (.D(WD3), .en(and_4_out), .Q(_3), .clk(Clk), .clr(Reset));
  Register #(.width(32)) register_5 (.D(WD3), .en(and_5_out), .Q(_4), .clk(Clk), .clr(Reset));
  Register #(.width(32)) register_6 (.D(WD3), .en(and_6_out), .Q(_5), .clk(Clk), .clr(Reset));
  Register #(.width(32)) register_7 (.D(WD3), .en(and_7_out), .Q(_6), .clk(Clk), .clr(Reset));
  Register #(.width(32)) register_8 (.D(WD3), .en(and_8_out), .Q(_7), .clk(Clk), .clr(Reset));
  Register #(.width(32)) register_9 (.D(WD3), .en(and_9_out), .Q(_8), .clk(Clk), .clr(Reset));
  Register #(.width(32)) register_10 (.D(WD3), .en(and_10_out), .Q(_9), .clk(Clk), .clr(Reset));
  Register #(.width(32)) register_11 (.D(WD3), .en(and_11_out), .Q(_10), .clk(Clk), .clr(Reset));
  Register #(.width(32)) register_12 (.D(WD3), .en(and_12_out), .Q(_11), .clk(Clk), .clr(Reset));
  Register #(.width(32)) register_13 (.D(WD3), .en(and_13_out), .Q(_12), .clk(Clk), .clr(Reset));
  Register #(.width(32)) register_14 (.D(WD3), .en(and_14_out), .Q(_13), .clk(Clk), .clr(Reset));
  Register #(.width(32)) register_15 (.D(WD3), .en(and_15_out), .Q(_14), .clk(Clk), .clr(Reset));
  Register #(.width(32)) register_16 (.D(WD3), .en(and_16_out), .Q(_15), .clk(Clk), .clr(Reset));
  Register #(.width(32)) register_17 (.D(WD3), .en(and_17_out), .Q(_16), .clk(Clk), .clr(Reset));
  Register #(.width(32)) register_18 (.D(WD3), .en(and_18_out), .Q(_17), .clk(Clk), .clr(Reset));
  Register #(.width(32)) register_19 (.D(WD3), .en(and_19_out), .Q(_18), .clk(Clk), .clr(Reset));
  Register #(.width(32)) register_20 (.D(WD3), .en(and_20_out), .Q(_19), .clk(Clk), .clr(Reset));
  Register #(.width(32)) register_21 (.D(WD3), .en(and_21_out), .Q(_20), .clk(Clk), .clr(Reset));
  Register #(.width(32)) register_22 (.D(WD3), .en(and_22_out), .Q(_21), .clk(Clk), .clr(Reset));
  Register #(.width(32)) register_23 (.D(WD3), .en(and_23_out), .Q(_22), .clk(Clk), .clr(Reset));
  Register #(.width(32)) register_24 (.D(WD3), .en(and_24_out), .Q(_23), .clk(Clk), .clr(Reset));
  Register #(.width(32)) register_25 (.D(WD3), .en(and_25_out), .Q(_24), .clk(Clk), .clr(Reset));
  Register #(.width(32)) register_26 (.D(WD3), .en(and_26_out), .Q(_25), .clk(Clk), .clr(Reset));
  Register #(.width(32)) register_27 (.D(WD3), .en(and_27_out), .Q(_26), .clk(Clk), .clr(Reset));
  Register #(.width(32)) register_28 (.D(WD3), .en(and_28_out), .Q(_27), .clk(Clk), .clr(Reset));
  Register #(.width(32)) register_29 (.D(WD3), .en(and_29_out), .Q(_28), .clk(Clk), .clr(Reset));
  Register #(.width(32)) register_30 (.D(WD3), .en(and_30_out), .Q(_29), .clk(Clk), .clr(Reset));
  Register #(.width(32)) register_31 (.D(WD3), .en(and_31_out), .Q(_30), .clk(Clk), .clr(Reset));
  Register #(.width(32)) register_32 (.D(WD3), .en(and_32_out), .Q(_31), .clk(Clk), .clr(Reset));
  Multiplexer #(.select(5), .width(32)) multiplexer_1 (
    .in0(_0), .in1(_1), .in2(_2), .in3(_3), .in4(_4), .in5(_5), .in6(_6), .in7(_7), .in8(_8), .in9(_9),
    .in10(_10), .in11(_11), .in12(_12), .in13(_13), .in14(_14), .in15(_15), .in16(_16), .in17(_17),
    .in18(_18), .in19(_19), .in20(_20), .in21(_21), .in22(_22), .in23(_23), .in24(_24), .in25(_25),
    .in26(_26), .in27(_27), .in28(_28), .in29(_29), .in30(_30), .in31(_31), .out(RD1), .sel(A1));  // open: en
  Multiplexer #(.select(5), .width(32)) multiplexer_2 (
    .in0(_0), .in1(_1), .in2(_2), .in3(_3), .in4(_4), .in5(_5), .in6(_6), .in7(_7), .in8(_8), .in9(_9),
    .in10(_10), .in11(_11), .in12(_12), .in13(_13), .in14(_14), .in15(_15), .in16(_16), .in17(_17),
    .in18(_18), .in19(_19), .in20(_20), .in21(_21), .in22(_22), .in23(_23), .in24(_24), .in25(_25),
    .in26(_26), .in27(_27), .in28(_28), .in29(_29), .in30(_30), .in31(_31), .out(RD2), .sel(A2));  // open: en

  // Other names for the same wires on the sheet: data[31:0] = WD3
endmodule

module ALU (
  input  [31:0] A,
  input  [31:0] B,
  input  [3:0] ALUOp,
  output [31:0] C,
  output zero
);

  wire [31:0] adder_1_out, or_1_out, subtractor_1_out;

  Adder #(.width(32)) adder_1 (.a(A), .b(B), .out(adder_1_out));  // open: cin, cout
  Subtractor #(.width(32)) subtractor_1 (.a(A), .b(B), .out(subtractor_1_out));  // open: bin, bout
  assign or_1_out = A | B;  // OR_Gate or_1, 32 bits wide
  Multiplexer #(.select(4), .width(32), .disabled(0)) multiplexer_1 (
    .in0(adder_1_out), .in1(subtractor_1_out), .in2(or_1_out), .out(C), .sel(ALUOp));  // open: in3, in4, in5, in6, in7, in8, in9, in10, in11, in12, in13, in14, in15, en
  Comparator #(.width(32)) comparator_1 (.a(C), .b({32{1'b0}}), .eq(zero));  // open: gt, lt
endmodule

module DM (
  input  [31:0] A,
  input  [31:0] WD,
  input  MemWrite,
  input  Clk,
  input  Reset,
  output [31:0] RD
);

  RAM #(.dataWidth(32), .bus("separate")) ram_1 (
    .addr(A[9:2]), .din(WD), .data(RD), .str(MemWrite), .clk(Clk), .clr(Reset));  // open: sel, ld
endmodule

module EXT (
  input  [15:0] Imm16,
  input  [1:0] ExtOp,
  output [31:0] Ext32
);

  wire [31:0] bit_extender_1_out, bit_extender_2_out;

  assign bit_extender_1_out = {{16{1'b0}}, Imm16};  // Bit_Extender bit_extender_1
  assign bit_extender_2_out = {{16{Imm16[15]}}, Imm16};  // Bit_Extender bit_extender_2
  Multiplexer #(.select(2), .width(32)) multiplexer_1 (
    .in0(bit_extender_1_out), .in1({Imm16, {16{1'b0}}}), .in2(bit_extender_2_out), .out(Ext32), .sel(ExtOp));  // open: in3, en
endmodule

module Controller (
  input  [5:0] Op,
  input  [5:0] Funct,
  output [1:0] RegDst,
  output ALUSrc,
  output MemtoReg,
  output RegWrite,
  output MemWrite,
  output Branch,
  output [1:0] ExtOp,
  output [3:0] ALUOp,
  output [1:0] Jump,
  output J
);

  wire addu, j_t, jalr, jr, nop, not_1_out, not_2_out, not_3_out, not_4_out, not_5_out, not_6_out, not_7_out,
       not_8_out, not_9_out, not_10_out, not_11_out, not_12_out, subu;

  not not_1 (not_1_out, Op[5]);
  not not_2 (not_2_out, Op[3]);
  not not_3 (not_3_out, Op[2]);
  not not_4 (not_4_out, Op[4]);
  not not_5 (not_5_out, Op[1]);
  not not_6 (not_6_out, Op[0]);
  not not_7 (not_7_out, Funct[5]);
  not not_8 (not_8_out, Funct[4]);
  not not_9 (not_9_out, Funct[3]);
  not not_10 (not_10_out, Funct[2]);
  not not_11 (not_11_out, Funct[0]);
  not not_12 (not_12_out, Funct[1]);
  and u_addu (addu, not_1_out, not_4_out, not_2_out, not_3_out, not_5_out, not_6_out, Funct[5], not_8_out, not_9_out, not_10_out, not_12_out, Funct[0]);
  and u_subu (subu, not_1_out, not_4_out, not_2_out, not_3_out, not_5_out, not_6_out, Funct[5], not_8_out, not_9_out, not_10_out, Funct[1], Funct[0]);
  and ori (ALUOp[1], not_1_out, not_4_out, Op[3], Op[2], not_5_out, Op[0]);
  and lw (MemtoReg, Op[5], not_4_out, not_2_out, not_3_out, Op[1], Op[0]);
  and sw (MemWrite, Op[5], not_4_out, Op[3], not_3_out, Op[1], Op[0]);
  and beq (Branch, not_1_out, not_4_out, not_2_out, Op[2], not_5_out, not_6_out);
  and lui (ExtOp[0], not_1_out, not_4_out, Op[3], Op[2], Op[1], Op[0]);
  and u_nop (nop, not_1_out, not_4_out, not_2_out, not_3_out, not_5_out, not_6_out, not_7_out, not_8_out, not_9_out, not_10_out, not_12_out, not_11_out);
  and u_j (j_t, not_1_out, not_4_out, not_2_out, not_3_out, Op[1], not_6_out);
  and jal (RegDst[1], not_1_out, not_4_out, not_2_out, not_3_out, Op[1], Op[0]);
  and u_jalr (jalr, not_1_out, not_4_out, not_2_out, not_3_out, not_5_out, not_6_out, not_7_out, not_8_out, Funct[3], not_10_out, not_12_out, Funct[0]);
  and u_jr (jr, not_1_out, not_4_out, not_2_out, not_3_out, not_5_out, not_6_out, not_7_out, not_8_out, Funct[3], not_10_out, not_12_out, not_11_out);
  or or_1 (Jump[1], jr, jalr, RegDst[1]);
  or or_2 (Jump[0], jr, jalr, j_t);
  or or_3 (J, jr, jalr, RegDst[1], j_t);
  or or_4 (ExtOp[1], MemtoReg, MemWrite);
  or or_5 (RegDst[0], addu, jalr, subu);
  or or_6 (ALUSrc, ALUOp[1], MemtoReg, MemWrite, ExtOp[0]);
  or or_7 (RegWrite, ALUOp[1], addu, subu, MemtoReg, ExtOp[0], RegDst[1]);
  or or_8 (ALUOp[0], subu, Branch);

  assign ALUOp[3:2] = 2'b00;

  // Other names for the same wires on the sheet: ori = ALUOp[1]; beq = Branch; lui = ExtOp[0]; lw = MemtoReg;
  //   jal = RegDst[1]; sw = MemWrite
endmodule

module IFU (
  input  PCSrc,
  input  J,
  input  Clk,
  input  Reset,
  input  [1:0] Jump,
  input  [31:0] j_r,
  output [31:0] PC_4,
  output [31:0] Instr
);

  wire [31:0] adder_2_out, adder_3_out, bit_extender_1_out, multiplexer_1_out, multiplexer_2_out,
       multiplexer_3_out, PC_q;

  assign bit_extender_1_out = {{14{1'b0}}, {Instr[15:0], 2'b00}};  // Bit_Extender bit_extender_1
  Adder #(.width(32)) adder_1 (.a(PC_q), .b(32'h4), .out(PC_4));  // open: cin, cout
  Adder #(.width(32)) adder_2 (.a(32'h4), .b(adder_3_out), .out(adder_2_out));  // open: cin, cout
  Adder #(.width(32)) adder_3 (.a(PC_q), .b(bit_extender_1_out), .out(adder_3_out));  // open: cin, cout
  // Probe on multiplexer_3_out
  // Probe on adder_2_out
  // Probe on PC_4
  Multiplexer #(.width(32)) multiplexer_1 (
    .in0(PC_4), .in1(adder_2_out), .out(multiplexer_1_out), .sel(PCSrc));  // open: en
  Multiplexer #(.width(32)) multiplexer_2 (
    .in0(multiplexer_1_out), .in1(multiplexer_3_out), .out(multiplexer_2_out), .sel(J));  // open: en
  Multiplexer #(.select(2), .width(32)) multiplexer_3 (
    .in0({Instr[31:28], Instr[25:0], 2'b00}), .in1({Instr[31:28], Instr[25:0], 2'b00}), .in2(j_r), .in3(j_r),
    .out(multiplexer_3_out), .sel(Jump));  // open: en
  Register #(.width(32)) PC (.D(multiplexer_2_out), .Q(PC_q), .clk(Clk), .clr(Reset));  // open: en
  ROM #(.addrWidth(5), .dataWidth(32)) rom_1 (.addr(PC_q[6:2]), .data(Instr));  // open: sel

  // Notes on the sheet:
  //   contents of rom_1 (hex, n*v repeats v):
  //   3c080004 3c090008 1288023 354affff 340b0004 34190000 ad6a0008 ad680004 ad690000 ac0a0000 8d6c0004
  //   8c0d0000 0 1094021 3c011000 34210001 321c821 0 3c01000c 34210000 1028fff8 1097823 8d780008
endmodule

module Datapth (
  input  in_1
);

  wire alu_1_zero, ALUSrc, Clk, controller_1_branch, MemtoReg, MemWrite, PCSrc, RegWrite;
  wire [1:0] ExtOp, RegDst;
  wire [3:0] ALUControl, ALUOp;
  wire [4:0] multiplexer_1_out;
  wire [31:0] alu_1_c, dm_1_rd, ext_1_ext32, grf_1_rd1, grf_1_rd2, ifu_1_p4, multiplexer_2_out,
       multiplexer_3_out;

  Clock clock_1 (.out(Clk));
  // IFU ifu_1: pin names not known; wires that end beside it: PCSrc, Clk, in_1, ifu_1_p4, ifu_1_p4[15:0]
  Multiplexer #(.width(5)) multiplexer_1 (
    .in0(ifu_1_p4[20:16]), .in1(ifu_1_p4[15:11]), .out(multiplexer_1_out), .sel(RegDst[0]));  // open: en
  EXT ext_1 (.Imm16(ifu_1_p4[15:0]), .ExtOp(ExtOp), .Ext32(ext_1_ext32));
  Controller controller_1 (
    .RegDst(RegDst), .ALUSrc(ALUSrc), .MemtoReg(MemtoReg), .RegWrite(RegWrite), .MemWrite(MemWrite),
    .Branch(controller_1_branch), .ExtOp(ExtOp), .ALUOp(ALUControl), .Op(ifu_1_p4[31:26]),
    .Funct(ifu_1_p4[5:0]));  // open: Jump, J
  GRF grf_1 (
    .A3(multiplexer_1_out), .WD3(multiplexer_3_out), .RD1(grf_1_rd1), .RD2(grf_1_rd2), .Clk(Clk),
    .Reset(in_1), .RegWrite(RegWrite), .A1(ifu_1_p4[25:21]), .A2(ifu_1_p4[20:16]));
  Multiplexer #(.width(32)) multiplexer_2 (
    .in0(grf_1_rd2), .in1(ext_1_ext32), .out(multiplexer_2_out), .sel(ALUSrc));  // open: en
  and and_1 (PCSrc, controller_1_branch, alu_1_zero);
  ALU alu_1 (.A(grf_1_rd1), .B(multiplexer_2_out), .C(alu_1_c), .zero(alu_1_zero), .ALUOp(ALUOp));
  DM dm_1 (.A(alu_1_c), .WD(grf_1_rd2), .MemWrite(MemWrite), .Clk(Clk), .Reset(in_1), .RD(dm_1_rd));
  Multiplexer #(.width(32)) multiplexer_3 (
    .in0(alu_1_c), .in1(dm_1_rd), .out(multiplexer_3_out), .sel(MemtoReg));  // open: en
  // Pins of 1 and 2 bits meet at RegDst

  // Other names for the same wires on the sheet: Reset = in_1
endmodule
