// Logisim project happymonth.circ as structural Verilog
module happymonth (
  input  [3:0] in_1,
  output out_2
);

  wire and_1_out, and_2_out, and_3_out, and_4_out, and_5_out, and_6_out, not_1_out, not_2_out, not_3_out,
       not_4_out;

  not not_1 (not_1_out, in_1[3]);
  not not_2 (not_2_out, in_1[2]);
  not not_3 (not_3_out, in_1[1]);
  not not_4 (not_4_out, in_1[0]);
  and and_1 (and_1_out, not_1_out, not_2_out, not_3_out, in_1[0]);
  and and_2 (and_2_out, not_1_out, in_1[2], not_3_out, not_4_out);
  and and_3 (and_3_out, not_1_out, in_1[2], not_3_out, in_1[0]);
  and and_4 (and_4_out, not_1_out, in_1[2], in_1[1], not_4_out);
  and and_5 (and_5_out, in_1[3], not_2_out, not_3_out, in_1[0]);
  and and_6 (and_6_out, in_1[3], not_2_out, in_1[1], not_4_out);
  or or_1 (out_2, and_1_out, and_2_out, and_3_out, and_4_out, and_5_out, and_6_out);
endmodule
