// Logisim project 4bit_sort.circ as structural Verilog
module _1bit_swap (
  input  I1,
  input  S,
  input  I2,
  output O1,
  output O2
);

  wire and_1_out, and_2_out, and_3_out, and_4_out, not_1_out, not_2_out;

  not not_1 (not_1_out, S);
  not not_2 (not_2_out, S);
  and and_1 (and_1_out, I1, not_1_out);
  and and_2 (and_2_out, S, I2);
  and and_3 (and_3_out, I1, S);
  and and_4 (and_4_out, not_2_out, I2);
  or or_1 (O1, and_1_out, and_2_out);
  or or_2 (O2, and_3_out, and_4_out);
endmodule

module _4bit_swap (
  input  [3:0] I1,
  input  in_2,
  input  [3:0] I2,
  output [3:0] O1,
  output [3:0] O2
);

  _1bit_swap u_1bit_swap_1 (.I1(I1[0]), .S(in_2), .I2(I2[0]), .O1(O1[0]), .O2(O2[0]));
  _1bit_swap u_1bit_swap_2 (.I1(I1[1]), .S(in_2), .I2(I2[1]), .O1(O1[1]), .O2(O2[1]));
  _1bit_swap u_1bit_swap_3 (.I1(I1[2]), .S(in_2), .I2(I2[2]), .O1(O1[2]), .O2(O2[2]));
  _1bit_swap u_1bit_swap_4 (.I1(I1[3]), .S(in_2), .I2(I2[3]), .O1(O1[3]), .O2(O2[3]));
endmodule

module _4bit_sort (
  input  [3:0] in_1,
  input  [3:0] in_2,
  input  [3:0] in_3,
  input  [3:0] in_4,
  output [3:0] out_5,
  output [3:0] out_6,
  output [3:0] out_7,
  output [3:0] out_8
);

  wire comparator_1_gt, comparator_2_gt, comparator_3_gt, comparator_4_gt, comparator_5_gt, comparator_6_gt;
  wire [3:0] n4bit_swap_1_o1, n4bit_swap_1_o2, n4bit_swap_2_o1, n4bit_swap_2_o2, n4bit_swap_3_o1,
       n4bit_swap_4_o1, n4bit_swap_4_o2, n4bit_swap_5_o1;

  Comparator #(.width(4), .mode("unsigned")) comparator_1 (.a(in_1), .b(in_2), .gt(comparator_1_gt));  // open: eq, lt
  Comparator #(.width(4), .mode("unsigned")) comparator_2 (
    .a(n4bit_swap_1_o2), .b(in_3), .gt(comparator_2_gt));  // open: eq, lt
  Comparator #(.width(4), .mode("unsigned")) comparator_3 (
    .a(n4bit_swap_2_o2), .b(in_4), .gt(comparator_3_gt));  // open: eq, lt
  _4bit_swap u_4bit_swap_1 (.I1(in_1), .in_2(comparator_1_gt), .I2(in_2), .O1(n4bit_swap_1_o1), .O2(n4bit_swap_1_o2));
  _4bit_swap u_4bit_swap_2 (
    .I1(n4bit_swap_1_o2), .in_2(comparator_2_gt), .I2(in_3), .O1(n4bit_swap_2_o1), .O2(n4bit_swap_2_o2));
  _4bit_swap u_4bit_swap_3 (.I1(n4bit_swap_2_o2), .in_2(comparator_3_gt), .I2(in_4), .O1(n4bit_swap_3_o1), .O2(out_8));
  _4bit_swap u_4bit_swap_4 (
    .I1(n4bit_swap_1_o1), .in_2(comparator_4_gt), .I2(n4bit_swap_2_o1), .O1(n4bit_swap_4_o1),
    .O2(n4bit_swap_4_o2));
  Comparator #(.width(4), .mode("unsigned")) comparator_4 (
    .a(n4bit_swap_1_o1), .b(n4bit_swap_2_o1), .gt(comparator_4_gt));  // open: eq, lt
  Comparator #(.width(4), .mode("unsigned")) comparator_5 (
    .a(n4bit_swap_4_o2), .b(n4bit_swap_3_o1), .gt(comparator_5_gt));  // open: eq, lt
  _4bit_swap u_4bit_swap_5 (
    .I1(n4bit_swap_4_o2), .in_2(comparator_5_gt), .I2(n4bit_swap_3_o1), .O1(n4bit_swap_5_o1), .O2(out_7));
  Comparator #(.width(4), .mode("unsigned")) comparator_6 (
    .a(n4bit_swap_4_o1), .b(n4bit_swap_5_o1), .gt(comparator_6_gt));  // open: eq, lt
  _4bit_swap u_4bit_swap_6 (.I1(n4bit_swap_4_o1), .in_2(comparator_6_gt), .I2(n4bit_swap_5_o1), .O1(out_5), .O2(out_6));
endmodule
