// Logisim project fibo.circ as structural Verilog: 1 circuit, main circuit main
module main (
  input  [2:0] in_1,
  output [3:0] out_2
);

  wire clock_1_out, comparator_1_lt, comparator_2_eq, comparator_2_gt, nor_1_out;
  wire [2:0] counter_1_q;
  wire [3:0] adder_1_out, register_1_q, register_2_q;

  Clock clock_1 (.out(clock_1_out));
  Counter #(.width(3), .max('h7), .ongoal("stay")) counter_1 (
    .Q(counter_1_q), .clk(clock_1_out));  // open: load, D, count, carry, clr
  Comparator #(.width(3), .mode("unsigned")) comparator_1 (
    .a(counter_1_q), .b(3'b001), .lt(comparator_1_lt));  // open: gt, eq
  Comparator #(.width(3), .mode("unsigned")) comparator_2 (
    .a(counter_1_q), .b(in_1), .gt(comparator_2_gt), .eq(comparator_2_eq));  // open: lt
  Register #(.width(4)) register_1 (.D(adder_1_out), .en(nor_1_out), .Q(register_1_q), .clk(clock_1_out));  // open: clr
  Register #(.width(4)) register_2 (
    .D(register_1_q), .en(nor_1_out), .Q(register_2_q), .clk(clock_1_out));  // open: clr
  nor nor_1 (nor_1_out, comparator_2_gt, comparator_2_eq);
  Adder #(.width(4)) adder_1 (
    .a(register_1_q), .b(register_2_q), .out(adder_1_out), .cin(comparator_1_lt));  // open: cout
  Multiplexer #(.width(4)) multiplexer_1 (.in0(register_1_q), .in1(4'b0000), .out(out_2), .sel(nor_1_out));  // open: en
endmodule
