// Logisim project mod5.circ as structural Verilog
module mod5 (
  input  In,
  output S0,
  output S1,
  output S2,
  output S3,
  output S4
);

  wire clock_1_out, not_1_out, not_2_out, not_3_out, not_4_out;
  wire [1:0] register_1_q, trans_1_out_3;

  trans trans_1 (.in_1(In), .in_2(register_1_q[0]), .out_3(trans_1_out_3));
  Register #(.width(2)) register_1 (.D(trans_1_out_3), .Q(register_1_q), .clk(clock_1_out));  // open: en, clr
  Clock clock_1 (.out(clock_1_out));
  // Probe on trans_1_out_3
  not not_1 (not_1_out, trans_1_out_3[0]);
  not not_2 (not_2_out, trans_1_out_3[1]);
  not not_3 (not_3_out, trans_1_out_3[1]);
  not not_4 (not_4_out, trans_1_out_3[0]);
  and and_1 (S1, not_1_out, not_2_out);
  and and_2 (S2, trans_1_out_3[0], not_3_out);
  and and_3 (S3, trans_1_out_3[0], trans_1_out_3[1]);
  and and_4 (S4, not_4_out, trans_1_out_3[1]);

  assign S0 = 1'b0;
endmodule

module trans (
  input  in_1,
  input  in_2,
  output [1:0] out_3
);


  assign out_3 = {in_2, in_1};
endmodule
